// Logisim project Half-heder.circ as structural Verilog: 1 circuit, main circuit main
module main (
  input  A,
  input  B,
  output SOM,
  output CARRY
);

  xor xor_1 (SOM, A, B);
  and and_1 (CARRY, B, A);
endmodule
