// Logisim project ns.circ as structural Verilog: 1 circuit, main circuit main
module main (
  input  in_1,
  input  in_2,
  input  in_3,
  input  in_4,
  input  in_5,
  input  in_6,
  input  in_7,
  input  in_8,
  input  in_9,
  output out_10,
  output out_11,
  output out_12,
  output out_13,
  output out_14
);

  wire main_1_carr_out, main_2_carr_out, main_3_carr_out;

  full_adder_main main_1 (.A(in_1), .B(in_2), .Carry_in(in_3), .R(out_10), .Carr_Out(main_1_carr_out));
  full_adder_main main_2 (.A(main_1_carr_out), .B(in_4), .Carry_in(in_5), .R(out_11), .Carr_Out(main_2_carr_out));
  full_adder_main main_3 (.A(main_2_carr_out), .B(in_6), .Carry_in(in_7), .R(out_12), .Carr_Out(main_3_carr_out));
  full_adder_main main_4 (.A(main_3_carr_out), .B(in_8), .Carry_in(in_9), .R(out_13), .Carr_Out(out_14));
endmodule
