// Logisim project somador.circ as structural Verilog: 1 circuit, main circuit main
module main (
  input  B3,
  input  B2,
  input  B1,
  input  B0,
  input  A3,
  input  A2,
  input  A1,
  input  A0,
  input  N_ADDDSUB,
  output R0,
  output R1,
  output R2,
  output R3,
  output C,
  output O
);

  wire and_1_out, and_2_out, multiplexer_1_out, multiplexer_2_out, multiplexer_3_out, multiplexer_4_out,
       not_1_out, not_2_out, not_3_out, not_4_out, not_5_out, not_6_out, not_7_out;

  not not_1 (not_1_out, B0);
  not not_2 (not_2_out, B1);
  not not_3 (not_3_out, B2);
  not not_4 (not_4_out, B3);
  Multiplexer multiplexer_1 (.in0(B0), .in1(not_1_out), .out(multiplexer_1_out), .sel(N_ADDDSUB));  // open: en
  Multiplexer multiplexer_2 (.in0(B1), .in1(not_2_out), .out(multiplexer_2_out), .sel(N_ADDDSUB));  // open: en
  Multiplexer multiplexer_3 (.in0(B2), .in1(not_3_out), .out(multiplexer_3_out), .sel(N_ADDDSUB));  // open: en
  Multiplexer multiplexer_4 (.in0(B3), .in1(not_4_out), .out(multiplexer_4_out), .sel(N_ADDDSUB));  // open: en
  ns_main main_1 (
    .in_1(N_ADDDSUB), .in_2(A0), .in_3(multiplexer_1_out), .in_4(A1), .in_5(multiplexer_2_out), .in_6(A2),
    .in_7(multiplexer_3_out), .in_8(A3), .in_9(multiplexer_4_out), .out_10(R0), .out_11(R1), .out_12(R2),
    .out_13(R3), .out_14(C));
  not not_5 (not_5_out, multiplexer_4_out);
  not not_6 (not_6_out, multiplexer_4_out);
  not not_7 (not_7_out, R3);
  and and_1 (and_1_out, not_5_out, not_6_out, R3);
  or or_1 (O, and_1_out, and_2_out);
  and and_2 (and_2_out, A3, multiplexer_4_out, not_7_out);
endmodule
