// Logisim project Unidade aritemica.circ as structural Verilog: 1 circuit, main circuit main
module main (
  input  B3,
  input  B2,
  input  B1,
  input  B0,
  input  A3,
  input  A2,
  input  A1,
  input  A0,
  input  Cin_Bin,
  input  OP__N_ADD_SUB,
  output Cout_Bout,
  output S3,
  output S2,
  output S1,
  output S0,
  output z,
  output N,
  output Ov,
  output out_19
);

  wire and_1_out, and_2_out, main_1_out_14, not_1_out, not_2_out, xor_1_out, xor_2_out, xor_3_out, xor_4_out,
       xor_5_out, xor_7_out, xor_8_out;

  xor xor_1 (xor_1_out, Cin_Bin, OP__N_ADD_SUB);
  xor xor_2 (xor_2_out, B2, OP__N_ADD_SUB);
  xor xor_3 (xor_3_out, B3, OP__N_ADD_SUB);
  xor xor_4 (xor_4_out, B1, OP__N_ADD_SUB);
  xor xor_5 (xor_5_out, B0, OP__N_ADD_SUB);
  ns_main main_1 (
    .in_1(xor_1_out), .in_2(A0), .in_3(xor_5_out), .in_4(A1), .in_5(xor_4_out), .in_6(A2), .in_7(xor_2_out),
    .in_8(A3), .in_9(xor_3_out), .out_10(S0), .out_11(S1), .out_12(S2), .out_13(N), .out_14(main_1_out_14));
  xor xor_6 (Cout_Bout, main_1_out_14, OP__N_ADD_SUB);
  xor xor_7 (xor_7_out, main_1_out_14, main_1_out_14);
  xor xor_8 (xor_8_out, A3, xor_3_out);
  not not_1 (not_1_out, Ov);
  not not_2 (not_2_out, N);
  nor nor_1 (z, S0, S1, S2, N);
  xor xor_9 (Ov, xor_7_out, xor_8_out);
  and and_1 (and_1_out, not_1_out, not_2_out);
  and and_2 (and_2_out, Ov, N);
  or or_1 (out_19, and_1_out, and_2_out);

  assign S3 = N;
endmodule
