// Logisim project full_adder.circ as structural Verilog: 1 circuit, main circuit main
module main (
  input  A,
  input  B,
  input  Carry_in,
  output R,
  output Carr_Out
);

  wire main_1_carry, main_1_som, main_2_carry;

  Half_heder_main main_1 (.A(A), .B(B), .SOM(main_1_som), .CARRY(main_1_carry));
  Half_heder_main main_2 (.A(main_1_carry), .B(Carry_in), .SOM(R), .CARRY(main_2_carry));
  or or_1 (Carr_Out, main_1_som, main_2_carry);
endmodule
